// Logisim project cpu_design.circ as structural Verilog: 17 circuits, main circuit FINAL
module main (
  input  INR_sc,
  input  clk,
  input  RST,
  output [15:0] output_main,
  output rB0
);

  wire AC_load, ACEq10, ADD, and_9_out, and_13_out, and_14_out, and_15_out, and_16_out, and_17_out, ANDop,
       AR_load, BSA, BUN, CLR_sc, D0, D1, D2, D3, D4, D5, D6, D7, DR, DREq10, E_clr, Eop, I, IR_load, n,
       not_1_out, not_2_out, not_3_out, or_1_out, p, PC_clear, PC_inc, r, rB1, rB2, rB3, rB4, rB5, rB6, rB7,
       rB8, rB9, rB10, rB11, rdEN, STA, T0, T1, T2, T3, T4, T5, T6, T7, w, wtEN, x1, x2, x3, x4, x5, x6, x7,
       y, z;
  wire [2:0] M2M1M0, S2S1S0;
  wire [15:0] common_bus_1_ir_output, DR_15_0;

  or or_1 (or_1_out, D0, D1, D2, D6);
  and and_1 (BUN, T4, D4);
  and and_2 (BSA, T5, D5);
  and and_3 (n, D5, T4);
  and and_4 (y, or_1_out, T4);
  buf or_2 (E_clr, rB10);  // OR_Gate
  buf or_3 (IR_load, T1);  // OR_Gate
  and and_5 (STA, D3, T4);
  and and_6 (DR, D2, T5);
  and and_7 (w, D6, T6);
  Controller controller_1 (
    .IR15_0(common_bus_1_ir_output), .DecodrEN2(1'b1), .Cntrl(T2), .clk1(clk), .INR_sc(INR_sc),
    .CLR_sc(CLR_sc), .decoder_INC(1'b1), .clk2(clk), .I(I), .D7(D7), .D6(D6), .D5(D5), .D4(D4), .D3(D3),
    .D2(D2), .D1(D1), .D0(D0), .T0(T0), .T1(T1), .T2(T2), .T3(T3), .T4(T4), .T5(T5), .T6(T6), .T7(T7), .r(r),
    .rB11(rB11), .rB10(rB10), .rB9(rB9), .rB8(rB8), .rB7(rB7), .rB6(rB6), .rB5(rB5), .rB4(rB4), .rB3(rB3),
    .rB2(rB2), .rB1(rB1), .rB0(rB0));
  Comparator #(.width(16)) comparator_1 (.a({16{1'b1}}), .b(output_main), .eq(ACEq10));  // open: gt, lt
  or or_4 (x1, BUN, BSA);
  or or_5 (x2, T0, n);
  or or_6 (x7, T1, z, y);
  buf or_7 (x5, T2);  // OR_Gate
  buf or_8 (x4, STA);  // OR_Gate
  or or_9 (x3, DR, w);
  or or_10 (rdEN, T1, z, y);
  and and_8 (p, D7, I, T3);
  busSelectGen busselectgen_1 (.x1(x1), .x3(x3), .x5(x5), .x7(x7), .x2(x2), .x6(x6), .x4(x4), .S2S1S0(S2S1S0));
  Comparator #(.width(16)) comparator_2 (.a({16{1'b1}}), .b(DR_15_0), .eq(DREq10));  // open: gt, lt
  and and_9 (and_9_out, D6, T5);
  and and_10 (ADD, D1, T5);
  not not_1 (not_1_out, D7);
  buf or_11 (PC_clear, RST);  // OR_Gate
  not not_2 (not_2_out, output_main[15]);
  not not_3 (not_3_out, Eop);
  and and_11 (z, not_1_out, I, T3);
  or or_12 (wtEN, STA, n, w);
  and and_12 (ANDop, D0, T5);
  and and_13 (and_13_out, w, DREq10);
  and and_14 (and_14_out, rB4, not_2_out);
  and and_15 (and_15_out, rB3, output_main[15]);
  and and_16 (and_16_out, rB2, ACEq10);
  and and_17 (and_17_out, rB1, not_3_out);
  or or_13 (AR_load, T0, T2, z);
  or or_14 (CLR_sc, BUN, BUN, DR, r, ANDop, ADD, p, STA, w);
  or or_15 (AC_load, ADD, rB9, rB7, rB6, DR, ANDop);
  ALUSelectGen aluselectgen_1 (
    .a1(ANDop), .a3(DR), .a5(rB9), .a7(rB6), .a2(ADD), .a6(rB7), .M2M1M0(M2M1M0));  // open: a4
  or or_16 (PC_inc, and_13_out, T1, and_14_out, and_15_out, and_16_out, and_17_out);
  common_bus common_bus_1 (
    .wtEN(wtEN), .rdEN(rdEN), .clk(clk), .AR_inc(n), .AR_load(AR_load), .S2S1S0(S2S1S0), .PC_inc(PC_inc),
    .PC_load(x1), .PC_clear(PC_clear), .DR_inc(and_9_out), .DR_load(y), .ALUselect(M2M1M0), .comE(rB8),
    .Eload(ADD), .Eclear(rB10), .AC_inc(rB5), .AC_load(AC_load), .AC_clear(rB11), .IR_load(IR_load),
    .DR_output(DR_15_0), .Eop(Eop), .AC_output(output_main), .IR_output(common_bus_1_ir_output));  // open: AR_clear, DR_clear, INPR, TR_inc, TR_load, TR_clear

  // Other names for the same wires on the sheet: AC_15_0[15:0] = output_main; AC_15 = output_main[15]
endmodule

module register_AR (
  input  [11:0] Input1,
  input  Increment,
  input  Load,
  input  Clear,
  input  clk,
  output [11:0] Output1
);

  wire [11:0] adder_1_out, multiplexer_1_out, multiplexer_2_out, multiplexer_3_out;

  Multiplexer #(.width(12)) multiplexer_1 (.in0(Output1), .in1(adder_1_out), .out(multiplexer_1_out), .sel(Increment));
  Multiplexer #(.width(12)) multiplexer_2 (.in0(multiplexer_1_out), .in1(Input1), .out(multiplexer_2_out), .sel(Load));
  Multiplexer #(.width(12)) multiplexer_3 (
    .in0(multiplexer_2_out), .in1({12{1'b0}}), .out(multiplexer_3_out), .sel(Clear));
  Register #(.width(12)) register_1 (.D(multiplexer_3_out), .clk(clk), .Q(Output1));  // open: en, clr
  Adder #(.width(12)) adder_1 (.a(12'h1), .b(Output1), .out(adder_1_out), .cin(1'b0));  // open: cout
endmodule

module AR (
  input  [15:0] AR_input,
  input  AR_inc,
  input  AR_load,
  input  AR_clear,
  input  clk,
  output [15:0] AR_output,
  output [11:0] Address
);

  register_AR register_ar_1 (
    .Input1(AR_input[11:0]), .Increment(AR_inc), .Load(AR_load), .Clear(AR_clear), .clk(clk),
    .Output1(Address));

  assign AR_output = {4'b0000, Address};
endmodule

module register_PC (
  input  [11:0] Input1,
  input  Increment,
  input  Load,
  input  Clear,
  input  clk,
  output [11:0] Output1
);

  wire [11:0] adder_1_out, multiplexer_1_out, multiplexer_2_out, multiplexer_3_out;

  Multiplexer #(.width(12)) multiplexer_1 (.in0(Output1), .in1(adder_1_out), .out(multiplexer_1_out), .sel(Increment));
  Multiplexer #(.width(12)) multiplexer_2 (.in0(multiplexer_1_out), .in1(Input1), .out(multiplexer_2_out), .sel(Load));
  Multiplexer #(.width(12)) multiplexer_3 (
    .in0(multiplexer_2_out), .in1({12{1'b0}}), .out(multiplexer_3_out), .sel(Clear));
  Register #(.width(12)) register_1 (.D(multiplexer_3_out), .clk(clk), .Q(Output1));  // open: en, clr
  Adder #(.width(12)) adder_1 (.a(12'h1), .b(Output1), .out(adder_1_out), .cin(1'b0));  // open: cout
endmodule

module PC (
  input  [15:0] PC_input,
  input  PC_inc,
  input  PC_load,
  input  PC_clear,
  input  clk,
  output [15:0] PC_output
);

  register_PC register_pc_1 (
    .Input1(PC_input[11:0]), .Increment(PC_inc), .Load(PC_load), .Clear(PC_clear), .clk(clk),
    .Output1(PC_output[11:0]));

  assign PC_output[15:12] = 4'b0000;
endmodule

module DR (
  input  [15:0] DR_input,
  input  DR_inc,
  input  DR_load,
  input  DR_clear,
  input  clk,
  output [15:0] DR_output
);

  wire [15:0] adder_1_out, multiplexer_1_out, multiplexer_2_out, multiplexer_3_out;

  Multiplexer #(.width(16)) multiplexer_1 (.in0(DR_output), .in1(adder_1_out), .out(multiplexer_1_out), .sel(DR_inc));
  Multiplexer #(.width(16)) multiplexer_2 (
    .in0(multiplexer_1_out), .in1(DR_input), .out(multiplexer_2_out), .sel(DR_load));
  Multiplexer #(.width(16)) multiplexer_3 (
    .in0(multiplexer_2_out), .in1({16{1'b0}}), .out(multiplexer_3_out), .sel(DR_clear));
  Register #(.width(16)) register_1 (.D(multiplexer_3_out), .clk(clk), .Q(DR_output));  // open: en, clr
  Adder #(.width(16)) adder_1 (.a(16'h1), .b(DR_output), .out(adder_1_out), .cin(1'b0));  // open: cout
endmodule

module AC (
  input  [15:0] AC_input,
  input  AC_inc,
  input  AC_load,
  input  AC_clear,
  input  clk,
  output [15:0] AC_output
);

  wire [15:0] adder_1_out, multiplexer_1_out, multiplexer_2_out, multiplexer_3_out;

  Multiplexer #(.width(16)) multiplexer_1 (.in0(AC_output), .in1(adder_1_out), .out(multiplexer_1_out), .sel(AC_inc));
  Multiplexer #(.width(16)) multiplexer_2 (
    .in0(multiplexer_1_out), .in1(AC_input), .out(multiplexer_2_out), .sel(AC_load));
  Multiplexer #(.width(16)) multiplexer_3 (
    .in0(multiplexer_2_out), .in1({16{1'b0}}), .out(multiplexer_3_out), .sel(AC_clear));
  Register #(.width(16)) register_1 (.D(multiplexer_3_out), .clk(clk), .Q(AC_output));  // open: en, clr
  Adder #(.width(16)) adder_1 (.a(16'h1), .b(AC_output), .out(adder_1_out), .cin(1'b0));  // open: cout
endmodule

module IR (
  input  [15:0] IR_input,
  input  IR_load,
  input  clk,
  output [15:0] IR_output
);

  wire [15:0] multiplexer_1_out;

  Multiplexer #(.width(16)) multiplexer_1 (.in0(IR_output), .in1(IR_input), .out(multiplexer_1_out), .sel(IR_load));
  Register #(.width(16)) register_1 (.D(multiplexer_1_out), .clk(clk), .Q(IR_output));  // open: en, clr
endmodule

module TR (
  input  [15:0] TR_input,
  input  TR_inc,
  input  TR_load,
  input  TR_clear,
  input  clk,
  output [15:0] TR_output
);

  wire [15:0] adder_1_out, multiplexer_1_out, multiplexer_2_out, multiplexer_3_out;

  Multiplexer #(.width(16)) multiplexer_1 (.in0(TR_output), .in1(adder_1_out), .out(multiplexer_1_out), .sel(TR_inc));
  Multiplexer #(.width(16)) multiplexer_2 (
    .in0(multiplexer_1_out), .in1(TR_input), .out(multiplexer_2_out), .sel(TR_load));
  Multiplexer #(.width(16)) multiplexer_3 (
    .in0(multiplexer_2_out), .in1({16{1'b0}}), .out(multiplexer_3_out), .sel(TR_clear));
  Register #(.width(16)) register_1 (.D(multiplexer_3_out), .clk(clk), .Q(TR_output));  // open: en, clr
  Adder #(.width(16)) adder_1 (.a(16'h1), .b(TR_output), .out(adder_1_out), .cin(1'b0));  // open: cout
endmodule

module ALU (
  input  [15:0] AC,
  input  [15:0] DR,
  input  [15:0] INPR,
  input  [2:0] ALUSelect,
  input  IPRS,
  input  IPLS,
  output Cout,
  output [15:0] ALUout
);

  wire [15:0] adder_1_out, and_1_out, not_1_out;

  assign not_1_out = ~AC;  // NOT_Gate not_1, 16 bits wide
  assign and_1_out = AC & DR;  // AND_Gate and_1, 16 bits wide
  Adder #(.width(16)) adder_1 (.a(AC), .b(DR), .out(adder_1_out), .cin(1'b0), .cout(Cout));
  Multiplexer #(.select(3), .width(16)) multiplexer_1 (
    .in1(and_1_out), .in2(adder_1_out), .in3(DR), .in4(INPR), .in5(not_1_out), .in6({IPRS, AC[15:1]}),
    .in7({AC[14:0], IPLS}), .out(ALUout), .sel(ALUSelect));  // open: in0
endmodule

module E_ff (
  input  comE,
  input  E_ip,
  input  load,
  input  clear,
  input  clk,
  output E_ff_out
);

  wire multiplexer_1_out, multiplexer_2_out, multiplexer_3_out, not_1_out;

  not not_1 (not_1_out, E_ff_out);
  Multiplexer multiplexer_1 (.in0(E_ff_out), .in1(not_1_out), .out(multiplexer_1_out), .sel(comE));
  Multiplexer multiplexer_2 (.in0(multiplexer_1_out), .in1(E_ip), .out(multiplexer_2_out), .sel(load));
  Multiplexer multiplexer_3 (.in0(multiplexer_2_out), .in1(1'b0), .out(multiplexer_3_out), .sel(clear));
  D_Flip_Flop d_ff_1 (.D(multiplexer_3_out), .clk(clk), .Q(E_ff_out));  // open: Qn, preset, reset
endmodule

module common_bus (
  input  wtEN,
  input  rdEN,
  input  clk,
  input  AR_inc,
  input  AR_load,
  input  AR_clear,
  input  [2:0] S2S1S0,
  input  PC_inc,
  input  PC_load,
  input  PC_clear,
  input  DR_inc,
  input  DR_load,
  input  DR_clear,
  input  [15:0] INPR,
  input  [2:0] ALUselect,
  input  comE,
  input  Eload,
  input  Eclear,
  input  AC_inc,
  input  AC_load,
  input  AC_clear,
  input  IR_load,
  input  TR_inc,
  input  TR_load,
  input  TR_clear,
  output [15:0] DR_output,
  output Eop,
  output [15:0] AC_output,
  output [15:0] IR_output
);

  wire Cout;
  wire [11:0] ar_1_address;
  wire [15:0] ALUout, ar_1_ar_output, multiplexer_1_out, pc_1_pc_output, ram_1_dout, tr_1_tr_output;

  RAM #(.addrWidth(12), .asyncread("true"), .dataWidth(16)) ram_1 (
    .addr(ar_1_address), .we(wtEN), .oe(rdEN), .clk(clk), .din(multiplexer_1_out), .dout(ram_1_dout));
  AR ar_1 (
    .AR_input(multiplexer_1_out), .AR_inc(AR_inc), .AR_load(AR_load), .AR_clear(AR_clear), .clk(clk),
    .AR_output(ar_1_ar_output), .Address(ar_1_address));
  PC pc_1 (
    .PC_input(multiplexer_1_out), .PC_inc(PC_inc), .PC_load(PC_load), .PC_clear(PC_clear), .clk(clk),
    .PC_output(pc_1_pc_output));
  DR dr_1 (
    .DR_input(multiplexer_1_out), .DR_inc(DR_inc), .DR_load(DR_load), .DR_clear(DR_clear), .clk(clk),
    .DR_output(DR_output));
  ALU alu_1 (
    .AC(AC_output), .DR(DR_output), .INPR(INPR), .ALUSelect(ALUselect), .IPRS(Eop), .IPLS(Eop), .Cout(Cout),
    .ALUout(ALUout));
  E_ff e_ff_1 (.comE(comE), .E_ip(Cout), .load(Eload), .clear(Eclear), .clk(clk), .E_ff_out(Eop));
  AC ac_1 (
    .AC_input(ALUout), .AC_inc(AC_inc), .AC_load(AC_load), .AC_clear(AC_clear), .clk(clk),
    .AC_output(AC_output));
  IR ir_1 (.IR_input(multiplexer_1_out), .IR_load(IR_load), .clk(clk), .IR_output(IR_output));
  TR tr_1 (
    .TR_input(multiplexer_1_out), .TR_inc(TR_inc), .TR_load(TR_load), .TR_clear(TR_clear), .clk(clk),
    .TR_output(tr_1_tr_output));
  Multiplexer #(.select(3), .width(16)) multiplexer_1 (
    .in1(ar_1_ar_output), .in2(pc_1_pc_output), .in3(DR_output), .in4(AC_output), .in5(IR_output),
    .in6(tr_1_tr_output), .in7(ram_1_dout), .out(multiplexer_1_out), .sel(S2S1S0));  // open: in0

  // Other names for the same wires on the sheet: AC_out[15:0] = AC_output; DR_out[15:0] = DR_output; E_ff_out = Eop
endmodule

module Sequence_Counter (
  input  INR_sc,
  input  CLR_sc,
  input  decoder_INC,
  input  clk,
  output [15:0] TO_15
);

  wire [3:0] adder_1_out, multiplexer_1_out, multiplexer_2_out, register_1_q;

  Adder #(.width(4)) adder_1 (.a(register_1_q), .b(4'b0001), .out(adder_1_out), .cin(1'b0));  // open: cout
  Multiplexer #(.width(4)) multiplexer_1 (.in0(register_1_q), .in1(adder_1_out), .out(multiplexer_1_out), .sel(INR_sc));
  Multiplexer #(.width(4)) multiplexer_2 (
    .in0(multiplexer_1_out), .in1(4'b0000), .out(multiplexer_2_out), .sel(CLR_sc));
  Register #(.width(4)) register_1 (.D(multiplexer_2_out), .clk(clk), .Q(register_1_q));  // open: en, clr
  Decoder #(.select(4)) decoder_1 (
    .out0(TO_15[0]), .out1(TO_15[1]), .out2(TO_15[2]), .out3(TO_15[3]), .out4(TO_15[4]), .out5(TO_15[5]),
    .out6(TO_15[6]), .out7(TO_15[7]), .out8(TO_15[8]), .out9(TO_15[9]), .out10(TO_15[10]), .out11(TO_15[11]),
    .out12(TO_15[12]), .out13(TO_15[13]), .out14(TO_15[14]), .out15(TO_15[15]), .sel(register_1_q),
    .en(decoder_INC));
endmodule

module Controller (
  input  [15:0] IR15_0,
  input  DecodrEN2,
  input  Cntrl,
  input  clk1,
  input  INR_sc,
  input  CLR_sc,
  input  decoder_INC,
  input  clk2,
  output I,
  output D7,
  output D6,
  output D5,
  output D4,
  output D3,
  output D2,
  output D1,
  output D0,
  output T0,
  output T1,
  output T2,
  output T3,
  output T4,
  output T5,
  output T6,
  output T7,
  output r,
  output rB11,
  output rB10,
  output rB9,
  output rB8,
  output rB7,
  output rB6,
  output rB5,
  output rB4,
  output rB3,
  output rB2,
  output rB1,
  output rB0
);

  wire multiplexer_1_out, not_1_out;
  wire [15:8] sequence_counter_1_to_15;

  D_Flip_Flop d_ff_1 (.D(multiplexer_1_out), .clk(clk1), .Q(I));  // open: Qn, preset, reset
  Multiplexer multiplexer_1 (.in0(I), .in1(IR15_0[15]), .out(multiplexer_1_out), .sel(Cntrl));
  not not_1 (not_1_out, I);
  and and_1 (rB11, r, IR15_0[11]);
  and and_2 (rB10, r, IR15_0[10]);
  and and_3 (rB9, r, IR15_0[9]);
  and and_4 (rB8, r, IR15_0[8]);
  and and_5 (rB7, r, IR15_0[7]);
  and and_6 (rB6, r, IR15_0[6]);
  and and_7 (rB5, r, IR15_0[5]);
  and and_8 (rB4, r, IR15_0[4]);
  and and_9 (rB3, r, IR15_0[3]);
  and and_10 (rB2, r, IR15_0[2]);
  and and_11 (rB1, r, IR15_0[1]);
  and and_12 (rB0, r, IR15_0[0]);
  Decoder #(.select(3)) decoder_1 (
    .out0(D0), .out1(D1), .out2(D2), .out3(D3), .out4(D4), .out5(D5), .out6(D6), .out7(D7),
    .sel(IR15_0[14:12]), .en(DecodrEN2));
  Sequence_Counter sequence_counter_1 (
    .INR_sc(INR_sc), .CLR_sc(CLR_sc), .decoder_INC(decoder_INC), .clk(clk2),
    .TO_15({sequence_counter_1_to_15, T7, T6, T5, T4, T3, T2, T1, T0}));
  and and_13 (r, D7, not_1_out, T3);

  // Other names for the same wires on the sheet: B0 = IR15_0[0]; B1 = IR15_0[1]; B2 = IR15_0[2]; B3 = IR15_0[3];
  //   B4 = IR15_0[4]; B5 = IR15_0[5]; B6 = IR15_0[6]; B7 = IR15_0[7]; B8 = IR15_0[8]; B9 = IR15_0[9];
  //   B10 = IR15_0[10]; B11 = IR15_0[11]
endmodule

module ALUSelectGen (
  input  a1,
  input  a3,
  input  a5,
  input  a7,
  input  a2,
  input  a6,
  input  a4,
  output [2:0] M2M1M0
);

  or or_1 (M2M1M0[0], a1, a3, a5, a7);
  or or_2 (M2M1M0[1], a7, a2, a6, a3);
  or or_3 (M2M1M0[2], a7, a5, a6, a4);
endmodule

module busSelectGen (
  input  x1,
  input  x3,
  input  x5,
  input  x7,
  input  x2,
  input  x6,
  input  x4,
  output [2:0] S2S1S0
);

  or or_1 (S2S1S0[0], x1, x3, x5, x7);
  or or_2 (S2S1S0[1], x7, x2, x6, x3);
  or or_3 (S2S1S0[2], x7, x5, x6, x4);
endmodule

module FINAL (
  input  in_1,
  input  startpulse,
  output [15:0] out_3
);

  wire and_1_out, clk, INR_sc, not_1_out, or_1_out, rB0;

  not not_1 (not_1_out, rB0);
  Clock clock_1 (.out(clk));
  _7_Segment_Display u_7_segment_display_1 (.g(1'b1), .f(1'b1), .a(1'b1), .b(1'b1), .e(1'b1), .c(1'b1));  // open: d, dp
  and and_1 (and_1_out, not_1_out, INR_sc);
  _7_Segment_Display u_7_segment_display_2 (.f(1'b1), .e(1'b1), .d(1'b1));  // open: g, a, b, c, dp
  _7_Segment_Display u_7_segment_display_3 (.g(1'b1), .f(1'b1), .a(1'b1), .b(1'b1), .e(1'b1));  // open: d, c, dp
  D_Flip_Flop d_ff_1 (.D(or_1_out), .clk(clk), .Q(INR_sc));  // open: Qn, preset, reset
  or or_1 (or_1_out, startpulse, and_1_out);
  _7_Segment_Display u_7_segment_display_4 (.g(1'b1), .f(1'b1), .b(1'b1), .e(1'b1), .c(1'b1));  // open: a, d, dp
  main main_1 (.INR_sc(INR_sc), .clk(clk), .RST(in_1), .output_main(out_3), .rB0(rB0));
  _7_Segment_Display u_7_segment_display_5 (.g(1'b1), .f(1'b1), .a(1'b1), .b(1'b1), .e(1'b1), .c(1'b1));  // open: d, dp
  Hex_Digit_Display hex_digit_display_1 (.value(out_3[15:12]));  // open: dp
  Hex_Digit_Display hex_digit_display_2 (.value(out_3[11:8]));  // open: dp
  Hex_Digit_Display hex_digit_display_3 (.value(out_3[7:4]));  // open: dp
  Hex_Digit_Display hex_digit_display_4 (.value(out_3[3:0]));  // open: dp
endmodule
